# Fritzing sketch led_nano (saved by Fritzing 0.9.3b)
breadboards: 1

parts:
  LED1 = LED - 5mm [color="Red (633nm)" package="5 mm [THT]"]
  R3 = Resistor [tolerance=±5% resistance=220 package=THT]
  Part2 = Arduino Nano (Rev3.0)

nets:
  N1: LED1.cathode, R3.Pin_1
  N2: LED1.anode, Part2.D2
  N3: R3.Pin_0, Part2.GND
