# Fritzing sketch lightsensor_nano (saved by Fritzing 0.9.3b)
breadboards: 1

parts:
  R1 = Photocell (LDR) [package=THT]
  R2 = Resistor [tolerance=±5% resistance=1k package=THT]
  Part2 = Arduino Nano (Rev3.0)

nets:
  N1: R1.pin_0, R2.Pin_1, Part2.A0
  N2: R1.pin_1, Part2.5V
  N3: R2.Pin_0, Part2.GND
