# Fritzing sketch nightlight_nano (saved by Fritzing 0.9.3b)
breadboards: 1

parts:
  R1 = Photocell (LDR) [package=THT]
  R2 = Resistor [tolerance=±5% resistance=1k package=THT]
  LED1 = LED - 5mm [color="Red (633nm)" package="5 mm [THT]"]
  R3 = Resistor [tolerance=±5% resistance=220 package=THT]
  Part2 = Arduino Nano (Rev3.0)

nets:
  N1: R1.pin_0, R2.Pin_1, Part2.A0
  N2: R1.pin_1, Part2.5V
  N3: R2.Pin_0, R3.Pin_0, Part2.GND
  N4: LED1.cathode, Part2.D2
  N5: LED1.anode, R3.Pin_1
